# Fritzing sketch circut diagram (saved by Fritzing 0.9.3b)
circuit board: 8.46667cm x 5.64444cm
breadboards: 1

parts:
  U2 = ESP8266 NodeMCU LoLin module
  E1 = ESP32-Cam
  LCM1602_IIC1 = LCM1602 IIC [part_number="LCM1602 IIC" chip_label="LCM1602 IIC" package="DIP (Dual Inline) [THT]"]
  U3 = LCD-16X2 [package=lcd-16x2_noholes]
  VCC1 = 4 x AAA Battery Mount

nets:
  N1: U2.D1, LCM1602_IIC1.SCL
  N2: U2.D2, LCM1602_IIC1.SDA
  N3: U2.RX, E1.RX/GPIO_1
  N4: U2.TX, E1.TX/GPIO_3
  3.3V: E1.3.3V, LCM1602_IIC1.VCC, VCC1.-, VCC1.+
  GND: E1.GPIO_0, E1.GND, LCM1602_IIC1.GND
  VSS: LCM1602_IIC1.VSS, U3.VSS
  VDD: LCM1602_IIC1.VDD, U3.VDD
  N5: LCM1602_IIC1.V0, U3.VO
  N6: LCM1602_IIC1.RS, U3.RS
  N7: LCM1602_IIC1.RW, U3.R_W
  N8: LCM1602_IIC1.E, U3.E
  N9: LCM1602_IIC1.D0, U3.DB0
  N10: LCM1602_IIC1.D1, U3.DB1
  N11: LCM1602_IIC1.D2, U3.DB2
  N12: LCM1602_IIC1.D3, U3.DB3
  N13: LCM1602_IIC1.D4, U3.DB4
  N14: LCM1602_IIC1.D5, U3.DB5
  N15: LCM1602_IIC1.D6, U3.DB6
  N16: LCM1602_IIC1.D7, U3.DB7
  N17: LCM1602_IIC1.A, U3.A
  N18: LCM1602_IIC1.K, U3.K
  N19: LCM1602_IIC1.LED_A, LCM1602_IIC1.LED_B

custom parts:
  ESP8266 NodeMCU LoLin module: ESP8266 based NodeMCU
  LCM1602 IIC: I2C-Module to use a 1602 or 2004 LCD on with the wire.h libory Serial LCD Modul
